# Fritzing sketch circuit (saved by Fritzing 0.9.3b)
breadboards: 1

parts:
  C1 = Electrolytic Capacitor [capacitance=4.7mF package="100 mil [THT, electrolytic]"]
  Part1 = Arduino Uno (Rev3)
  R1 = Resistor [tolerance=±5% resistance=220 package=THT]
  R2 = Resistor [tolerance=±10% resistance=100 package=THT]
  D1 = SOLAR-IXYS [package=solarbit-12x1]

nets:
  N1: C1.-, Part1.VIN, R1.Pin_1, D1.A
  N2: C1.+, Part1.GND, R2.Pin_0, D1.C
  N3: Part1.A0, R1.Pin_0, R2.Pin_1
